# Fritzing sketch Shield (saved by Fritzing 0.9.1b)
circuit board: 8.37912cm x 8.97178cm

parts:
  GND1 = male pin header, 2 pins [form="♂ (male)"]
  GND2 = male pin header, 1 pin [form="♂ (male)"]
  RST = male pin header, 1 pin [form="♂ (male)"]  # not connected
  VCC1 = male pin header, 2 pins [form="♂ (male)"]
  GND = male alternating pin header, 16 pins [form="♂ (male)"]
  5V = male alternating pin header, 16 pins [form="♂ (male)"]
  3_3V = male alternating pin header, 16 pins [form="♂ (male)"]
  VCC0 = male alternating pin header, 3 pins [form="♂ (male)"]
  G3 = male alternating pin header, 8 pins [form="♂ (male)"]
  V3 = male alternating pin header, 8 pins [form="♂ (male)"]
  G9 = male alternating pin header, 16 pins [form="♂ (male)"]
  V9 = male alternating pin header, 16 pins [form="♂ (male)"]
  V10 = male alternating pin header, 16 pins [form="♂ (male)"]
  G10 = male pin header, 16 pins [form="♂ (male)"]
  JOY1 = male alternating pin header, 6 pins [form="♂ (male)"]
  G7 = male alternating pin header, 3 pins [form="♂ (male)"]
  V7 = male alternating pin header, 3 pins [form="♂ (male)"]
  G6 = male alternating pin header, 6 pins [form="♂ (male)"]
  V6 = male alternating pin header, 6 pins [form="♂ (male)"]
  GND0 = male pin header, 1 pin [form="♂ (male)"]
  V4 = male alternating pin header, 6 pins [form="♂ (male)"]
  G4 = male alternating pin header, 6 pins [form="♂ (male)"]
  J8''' = male alternating pin header, 4 pins [form="♂ (male)"]
  J8''''' = male alternating pin header, 4 pins [form="♂ (male)"]
  J8'' = male alternating pin header, 4 pins [form="♂ (male)"]
  I2C = male alternating pin header, 4 pins [form="♂ (male)"]
  J8' = male alternating pin header, 4 pins [form="♂ (male)"]
  J8'''' = male alternating pin header, 4 pins [form="♂ (male)"]
  J8'''''' = male alternating pin header, 4 pins [form="♂ (male)"]
  08_09_10_11_12_13_14_15 = male alternating pin header, 8 pins [form="♂ (male)"]  # not connected
  13_12_11_10_09_08 = male alternating pin header, 6 pins [form="♂ (male)"]  # not connected
  07_06_05_04_03_02 = male alternating pin header, 6 pins [form="♂ (male)"]  # not connected
  53_51_49_47_45_43_41_39_37_35_33_31_29_27_25_23 = male alternating pin header, 16 pins [form="♂ (male)"]  # not connected
  52_50_48_46_44_42_40_38_36_34_32_30_28_26_24_22 = male alternating pin header, 16 pins [form="♂ (male)"]  # not connected
  H2 = male pin header, 2 pins [form="♂ (male)"]
  H0 = male alternating pin header, 8 pins [form="♂ (male)"]
  17_18_19 = male pin header, 3 pins [form="♂ (male)"]
  DIN_CLK_LOAD = male pin header, 3 pins [form="♂ (male)"]
  17_18_19_2 = male alternating pin header, 3 pins [form="♂ (male)"]  # not connected
  7seg = male alternating pin header, 5 pins [form="♂ (male)"]
  JOY0 = male alternating pin header, 6 pins [form="♂ (male)"]

nets:
  N1: GND1.pin1, GND1.pin2, G9.pin1, G9.pin2, G9.pin3, G9.pin4, G9.pin5, G9.pin6, G9.pin7, G9.pin8, G9.pin9, G9.pin10, G9.pin11, G9.pin12, G9.pin13, G9.pin14, G9.pin15, G9.pin16, G10.pin1, G10.pin2, G10.pin3, G10.pin4, G10.pin5, G10.pin6, G10.pin7, G10.pin8, G10.pin9, G10.pin10, G10.pin11, G10.pin12, G10.pin13, G10.pin14, G10.pin15, G10.pin16, J8'''.pin3, J8'''''.pin3, J8''.pin3, I2C.pin3, J8'.pin3, J8''''.pin3, J8''''''.pin3, 7seg.pin5
  N2: GND2.pin1, GND.pin1, GND.pin2, GND.pin3, GND.pin4, GND.pin5, GND.pin6, GND.pin7, GND.pin8, GND.pin9, GND.pin10, GND.pin11, GND.pin12, GND.pin13, GND.pin14, GND.pin15, GND.pin16, VCC0.pin1, G3.pin1, G3.pin2, G3.pin3, G3.pin4, G3.pin5, G3.pin6, G3.pin7, G3.pin8, JOY1.pin5, JOY0.pin5
  N3: VCC1.pin1, VCC1.pin2, V9.pin1, V9.pin2, V9.pin3, V9.pin4, V9.pin5, V9.pin6, V9.pin7, V9.pin8, V9.pin9, V9.pin10, V9.pin11, V9.pin12, V9.pin13, V9.pin14, V9.pin15, V9.pin16, V10.pin1, V10.pin2, V10.pin3, V10.pin4, V10.pin5, V10.pin6, V10.pin7, V10.pin8, V10.pin9, V10.pin10, V10.pin11, V10.pin12, V10.pin13, V10.pin14, V10.pin15, V10.pin16, JOY1.pin6, V7.pin1, V7.pin2, V7.pin3, V6.pin1, V6.pin2, V6.pin3, V6.pin4, V6.pin5, V6.pin6, V4.pin1, V4.pin2, V4.pin3, V4.pin4, V4.pin5, V4.pin6, J8'''.pin4, J8'''''.pin4, J8''.pin4, I2C.pin4, J8'.pin4, J8''''.pin4, J8''''''.pin4, 7seg.pin1, JOY0.pin6
  N4: 5V.pin1, 5V.pin2, 5V.pin3, 5V.pin4, 5V.pin5, 5V.pin6, 5V.pin7, 5V.pin8, 5V.pin9, 5V.pin10, 5V.pin11, 5V.pin12, 5V.pin13, 5V.pin14, 5V.pin15, 5V.pin16, VCC0.pin2, V3.pin1, V3.pin2, V3.pin3, V3.pin4, V3.pin5, V3.pin6, V3.pin7, V3.pin8
  N5: 3_3V.pin1, 3_3V.pin2, 3_3V.pin3, 3_3V.pin4, 3_3V.pin5, 3_3V.pin6, 3_3V.pin7, 3_3V.pin8, 3_3V.pin9, 3_3V.pin10, 3_3V.pin11, 3_3V.pin12, 3_3V.pin13, 3_3V.pin14, 3_3V.pin15, 3_3V.pin16, VCC0.pin3
  N6: JOY1.pin1, H0.pin5
  N7: JOY1.pin2, H0.pin6
  N8: JOY1.pin3, H0.pin7
  N9: JOY1.pin4, H0.pin8
  N10: G7.pin1, G7.pin2, G7.pin3, G6.pin1, G6.pin2, G6.pin3, G6.pin4, G6.pin5, G6.pin6, GND0.pin1, G4.pin1, G4.pin2, G4.pin3, G4.pin4, G4.pin5, G4.pin6
  N11: J8'''.pin1, J8'''''.pin1, J8''.pin1, I2C.pin1, J8'.pin1, J8''''.pin1, J8''''''.pin1, H2.pin1
  N12: J8'''.pin2, J8'''''.pin2, J8''.pin2, I2C.pin2, J8'.pin2, J8''''.pin2, J8''''''.pin2, H2.pin2
  N13: H0.pin1, JOY0.pin1
  N14: H0.pin2, JOY0.pin2
  N15: H0.pin3, JOY0.pin3
  N16: H0.pin4, JOY0.pin4
  N17: 17_18_19.pin1, DIN_CLK_LOAD.pin1, 7seg.pin2
  N18: 17_18_19.pin2, DIN_CLK_LOAD.pin2, 7seg.pin3
  N19: 17_18_19.pin3, DIN_CLK_LOAD.pin3, 7seg.pin4

notes:
  Kerbal Space Program
  for
  by
  KAPCOM
  lawnmowerlatte
  version 1.0
  02
  03
  04
  05
  06
  07
  08
  09
  10
  11
  12
  13
  17
  18
  19
  A8
  A9
  A10
  A11
  A12
  A13
  A14
  A15
  52
  24
  26
  28
  30
  34
  32
  38
  36
  50
  48
  40
  42
  44
  46
  51
  43
  47
  35
  37
  33
  53
  41
  31
  39
  27
  45
  49
  25
  29
  23
  22
